# Fritzing sketch Controler V2 (saved by Fritzing 0.7.10b)
perfboards: 1

parts:
  LCD1 = LCD screen  # not connected
  S1 = Pushbutton [package="[THT]"]  # not connected
  S2 = Pushbutton [package="[THT]"]  # not connected
  LED1 = RGB LED (com. anode, rbg) [package="5 mm [THT]"]  # not connected
  LED2 = RGB LED (com. anode, rbg) [package="5 mm [THT]"]  # not connected
  LED3 = RGB LED (com. anode, rbg) [package="5 mm [THT]"]  # not connected
  LED4 = RGB LED (com. anode, rbg) [package="5 mm [THT]"]  # not connected
  LED5 = RGB LED (com. anode, rbg) [package="5 mm [THT]"]  # not connected
  T1 = LM35 Temperature Sensor [package="TO92 [THT]"]  # not connected
  R1 = Photocell (LDR) [package=THT]  # not connected
  J1 = Piezo Speaker  # not connected
  S3 = Pushbutton [package="[THT]"]
  S4 = Pushbutton [package="[THT]"]  # not connected
  S5 = Pushbutton [package="[THT]"]  # not connected
  S6 = Pushbutton [package="[THT]"]  # not connected
  S7 = Pushbutton [package="[THT]"]  # not connected
  ENCODER1 = Rotary Encoder with Knob  # not connected

nets:
  N1: S3.Pin_1, S3.Pin_2
  N2: S3.Pin_3, S3.Pin_4

custom parts:
  Rotary Encoder with Knob: Rotary Encoder with 1/4" Shaft and Knob
