# Fritzing sketch controler interface (saved by Fritzing 0.7.10b)
perfboards: 1

parts:
  RE1 = Rotary Encoder [package=THT]  # not connected
  S1 = Pushbutton [package="[THT]"]
  J1 = Piezo Speaker  # not connected
  LCD1 = LCD screen  # not connected
  VCC1 = Battery block 9V  # not connected
  CONN1 = USB connector [package=THT]
  U1 = microSD Socket [package="Molex 502774-0891 [SMD]"]  # not connected
  LED2 = Super Flux LED blue [color=Blue]  # not connected
  LED3 = Super Flux LED blue [color=Blue]  # not connected
  LED4 = Super Flux RGB LED (com. anode) [color=Blue]  # not connected
  LED5 = Super Flux LED blue [color=Blue]  # not connected
  LED6 = Super Flux RGB LED (com. anode) [color=Blue]  # not connected
  S2 = Pushbutton [package="[THT]"]
  S3 = Pushbutton [package="[THT]"]
  S4 = Pushbutton [package="[THT]"]
  S5 = Pushbutton [package="[THT]"]
  S6 = Pushbutton [package="[THT]"]
  S7 = Pushbutton [package="[THT]"]

nets:
  N1: S1.Pin_1, S1.Pin_2
  N2: S1.Pin_3, S1.Pin_4
  N3: CONN1.GND, CONN1.chassis5, CONN1.chassis6
  N4: S2.Pin_1, S2.Pin_2
  N5: S2.Pin_3, S2.Pin_4
  N6: S3.Pin_1, S3.Pin_2
  N7: S3.Pin_3, S3.Pin_4
  N8: S4.Pin_1, S4.Pin_2
  N9: S4.Pin_3, S4.Pin_4
  N10: S5.Pin_1, S5.Pin_2
  N11: S5.Pin_3, S5.Pin_4
  N12: S6.Pin_1, S6.Pin_2
  N13: S6.Pin_3, S6.Pin_4
  N14: S7.Pin_1, S7.Pin_2
  N15: S7.Pin_3, S7.Pin_4
