# Fritzing sketch Complete Schmatic (saved by Fritzing 0.8.7b)
circuit board: 9cm x 11cm

parts:
  U1 = atmega328 [part_number=ATMEGA328P-PU package=dip]
  U2 = Voltage Regulator - 5V [part_number=LM7805 package="TO220 [THT]"]
  Power_plug1 = Power plug
  S1 = Toggle Switch [package=THT]
  D1 = Rectifier Diode [part_number=1N4001 package="300 mil [THT]"]
  C1 = Electrolytic Capacitor [capacitance=0.1mF voltage=50V package="100 mil [THT, electrolytic]"]
  C2 = Electrolytic Capacitor [capacitance=10µF voltage=50V package="100 mil [THT, electrolytic]"]
  XTAL1 = Crystal [frequency="16 Mhz" package=THT]
  C3 = Ceramic Capacitor [capacitance=22pF voltage=50V package="100 mil [THT, multilayer]"]
  C4 = Ceramic Capacitor [capacitance=22pF voltage=50V package="100 mil [THT, multilayer]"]
  S2 = Pushbutton [package="[THT]"]
  R1 = Resistor [tolerance=±5% resistance=10k package=THT]
  J1 = double row female pin header, 6 pins [form="♀ (female)"]
  LCD1 = LCD screen
  R2 = Trimmer Potentiometer [maximum_resistance=10kΩ package=THT]
  J2 = female pin header, 4 pins [form="♀ (female)"]
  J3 = female pin header, 4 pins [form="♀ (female)"]
  R3 = Resistor [tolerance=±5% resistance=220 package=THT]
  LED1 = LED - 5mm [color="Red (633nm)" package="5 mm [THT]"]
  R4 = Resistor [tolerance=±5% resistance=220 package=THT]
  LED2 = LED - 5mm [color="Red (633nm)" package="5 mm [THT]"]
  R5 = Resistor [tolerance=±5% resistance=220 package=THT]
  LED3 = LED - 5mm [color="Red (633nm)" package="5 mm [THT]"]
  T1 = LM35 Temperature Sensor [package="TO92 [THT]"]
  R6 = Resistor [tolerance=±5% resistance=10k package=THT]
  R7 = Photocell (LDR) [package=THT]
  MIC1 = Microphone
  C5 = Ceramic Capacitor [capacitance=100nF voltage=50V package="100 mil [THT, multilayer]"]
  R8 = Resistor [tolerance=±5% resistance=10k package=THT]
  R9 = Resistor [tolerance=±5% resistance=100k package=THT]
  R10 = Resistor [tolerance=±5% resistance=10k package=THT]
  Q1 = NPN-Transistor [part_number=2N3904 package="TO92 [THT]"]
  S3 = Pushbutton [package="[THT]"]
  S4 = Pushbutton [package="[THT]"]
  S5 = Pushbutton [package="[THT]"]
  R11 = Resistor [tolerance=±5% resistance=10k package=THT]
  R12 = Resistor [tolerance=±5% resistance=10k package=THT]
  R13 = Resistor [tolerance=±5% resistance=10k package=THT]

nets:
  N1: U1.RESET, S2.Pin_1, S2.Pin_2, R1.Pin_0, J1.pin3
  N2: U1.D0_(RX), J2.pin3
  N3: U1.D1_(TX), J2.pin4
  N4: U1.D2, LCD1.RS
  N5: U1.D3_(PWM), LCD1.E
  N6: U1.D4, LCD1.DB4
  5V: U1.VCC, U1.AVCC, U1.AREF, U2.output_voltage, C2.+, R1.Pin_1, J1.pin6, LCD1.VDD, LCD1.LED+, R2.leg1, J2.pin1, T1.+Vs, R7.pin_0, R8.Pin_1, R10.Pin_1, S3.Pin_1, S3.Pin_2, S4.Pin_1, S4.Pin_2, S5.Pin_1, S5.Pin_2
  GND: U1.GND, U2.GND, Power_plug1.GND, C1.-, C2.-, C3.0, C4.0, S2.Pin_3, S2.Pin_4, J1.pin4, LCD1.VSS, LCD1.R/W, LCD1.LED-, R2.leg2, J2.pin2, J3.pin1, LED1.cathode, LED2.cathode, LED3.cathode, T1.GND, R6.Pin_1, MIC1.pin1, Q1.E, R11.Pin_1, R12.Pin_1, R13.Pin_1
  N7: U1.XLAT1, XTAL1.pin_0, C3.1
  N8: U1.XLAT2, XTAL1.pin_1, C4.1
  N9: U1.D5_(PWM), LCD1.DB5
  N10: U1.D6_(PWM), LCD1.DB6
  N11: U1.D7, LCD1.DB7
  N12: U1.D8, J3.pin4, R3.Pin_0
  N13: U1.D9_(PWM), J3.pin3, R4.Pin_0
  N14: U1.D10_(PWM), J3.pin2, R5.Pin_0
  N15: U1.D11_(PWM), J1.pin5
  N16: U1.D12, J1.pin1
  N17: U1.D13, J1.pin2
  N18: U1.A0, T1.Vout
  N19: U1.A1, R6.Pin_0, R7.pin_1
  N20: U1.A2, R8.Pin_0, R9.Pin_1, Q1.C
  N21: U1.A3, S5.Pin_3, S5.Pin_4, R13.Pin_0
  N22: U1.A4, S4.Pin_3, S4.Pin_4, R12.Pin_0
  N23: U1.A5, S3.Pin_3, S3.Pin_4, R11.Pin_0
  N24: U2.input_voltage, D1.cathode, C1.+
  N25: Power_plug1.VCC, S1.COM
  N26: S1.L1, D1.anode
  N27: LCD1.V0, R2.wiper
  N28: R3.Pin_1, LED1.anode
  N29: R4.Pin_1, LED2.anode
  N30: R5.Pin_1, LED3.anode
  N31: MIC1.pin2, C5.0, R10.Pin_0
  N32: C5.1, R9.Pin_0, Q1.B

notes:
  MISO
  SCK
  RESET
  GND
  MOSI
  VCC
  TX
  RX
  Out 1
  Out 2
  Out 3
