# Fritzing sketch Fritzing sample (saved by Fritzing 0.8.3b)
breadboards: 1

parts:
  T1 = LM35 Temperature Sensor [package="TO92 [THT]"]
  LCD1 = LCD screen  # not connected
  MIC1 = Microphone  # not connected
  R1 = Photocell (LDR) [package=THT]
  U1 = LM 358 Dual Op-Amp [package="DIP8 [THT]"]  # not connected
  U2 = atmega328 [package=dip]
  Power_plug1 = Power plug
  XTAL1 = Crystal [frequency="16 Mhz" package=THT]
  U3 = Voltage Regulator - 5V [part_number=LM7805 package="TO220 [THT]"]
  C2 = Ceramic Capacitor [capacitance=10pF package="100 mil [THT, multilayer]"]
  C3 = Ceramic Capacitor [capacitance=10pF package="100 mil [THT, multilayer]"]
  C4 = Electrolytic Capacitor [capacitance=10µF package="100 mil [THT, electrolytic]"]
  C5 = Ceramic Capacitor [capacitance=100nF package="100 mil [THT, multilayer]"]
  R2 = Resistor [tolerance=±5% resistance=10k package=THT]
  R3 = Resistor [tolerance=±5% resistance=10k package=THT]

nets:
  N1: T1.+Vs, R1.pin_1, U2.VCC, U2.AVCC, U2.AREF, U3.output_voltage, C4.+, C5.1, R2.Pin_1
  N2: T1.Vout, U2.A1
  GND: T1.GND, U2.GND, Power_plug1.GND, U3.GND, C2.1, C3.0, C4.-, C5.0, R3.Pin_0
  N3: R1.pin_0, U2.A0, R3.Pin_1
  N4: U2.RESET, R2.Pin_0
  N5: U2.XLAT1, XTAL1.pin_1, C3.1
  N6: U2.XLAT2, XTAL1.pin_0, C2.0
  N7: Power_plug1.VCC, U3.input_voltage
